# Fritzing sketch bikesafetyfritz (saved by Fritzing 0.9.4)
breadboards: 1

parts:
  Argon1 = Particle Argon
  HC-SR04_Sensor_1 = HC-SR04 Ultrasonic Distance Sensor
  R1 = Resistor [tolerance=±5% resistance=220 package=THT]
  U3 = GPS6MV2 [package=GSP6MV2]
  Part1 = Adafruit MicroSD card breakout board [part_number="Adafruit #254"]

nets:
  GND: Argon1.GND, HC-SR04_Sensor_1.GND, U3.GND, Part1.GND
  N1: Argon1.RX, U3.RX-I
  N2: Argon1.TX, U3.TX-O
  N3: Argon1.D5, R1.Pin_0
  VCC: Argon1.LI+, HC-SR04_Sensor_1.VCC, U3.VCC, Part1.+3V3
  N4: HC-SR04_Sensor_1.ECHO, R1.Pin_1

custom parts:
  Particle Argon: The Argon is a powerful Wi-Fi enabled development board that can act as either a standalone Wi-Fi endpoint or Wi-Fi enabled gateway for Particle Mesh networks. It is based on the Nordic nRF52840 and has built-in battery charging circuitry so it’s easy to connect a Li-Po and deploy your local network in minutes. The Argon is great for connecting existing projects to the Particle Device Cloud or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
  GPS6MV2: GPS transciever
  Adafruit MicroSD card breakout board: Not just a simple breakout board, this microSD adapter goes the extra mile - designed for ease of use. Onboard 5v->3v regulator provides 150mA for power-hungry cards 3v level shifting means you can use this with ease on either 3v or 5v systems Uses a proper level shifting chip, not resistors: less problems, and faster read/write access Use 3 or 4 digital pins to read and write 2Gb+ of storage!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
